# Fritzing sketch drums (saved by Fritzing 0.7.12b)
breadboards: 1

parts:
  Arduino1 = Arduino
  R1 = 10k Ω Resistor [package=THT]
  J1 = Piezo Speaker
  J2 = Piezo Speaker
  J3 = Piezo Speaker
  R2 = 10k Ω Resistor [package=THT]
  R3 = 10k Ω Resistor [package=THT]
  J4 = Piezo Speaker
  R4 = 10k Ω Resistor [package=THT]

nets:
  N1: Arduino1.D11, J4.pin2, R4.Pin_0
  N2: Arduino1.D10, J3.pin2, R3.Pin_0
  N3: Arduino1.D9, J2.pin2, R2.Pin_0
  N4: Arduino1.D8, R1.Pin_0, J1.pin2
  N5: Arduino1.GND, R1.Pin_1, J1.pin1, J2.pin1, J3.pin1, R2.Pin_1, R3.Pin_1, J4.pin1, R4.Pin_1
