# Fritzing sketch guitar (saved by Fritzing 0.7.12b)
breadboards: 1

parts:
  Arduino1 = Arduino
  R1 = Slide Potentiometer [maximum_resistance=100kΩ]
  R2 = Resistor [tolerance=±5% resistance=220 package=THT]

nets:
  N1: Arduino1.+5V, R1.leg1
  N2: Arduino1.GND, R1.leg2, R2.Pin_1
  N3: Arduino1.A0, R1.wiper, R2.Pin_0
