# Fritzing sketch maracas (saved by Fritzing 0.7.12b)
breadboards: 1

parts:
  Arduino1 = Arduino
  R2 = 10k Ω Resistor [package=THT]
  S1 = Tilt Switch [package=THT]
  R3 = 10k Ω Resistor [package=THT]
  S2 = Tilt Switch [package=THT]

nets:
  N1: Arduino1.D7, R3.Pin_0, S2.Pin_1
  N2: Arduino1.D6, R2.Pin_0, S1.Pin_1
  N3: Arduino1.+5V, S1.Pin_2, S2.Pin_2
  N4: Arduino1.GND, R2.Pin_1, R3.Pin_1
